// Logisim project 1 bit ALU.circ as structural Verilog: 1 circuit, main circuit 1 bit ALU
module _1_bit_ALU (
  input  Cin,
  input  A,
  input  B,
  input  [2:0] OPCODE,
  output Cout_Bout_Mout,
  output RESULT
);

  wire adder_1_cout, adder_1_out, and_1_out, comparator_1_eq, comparator_1_gt, comparator_1_lt,
       multiplier_1_cout, multiplier_1_out, or_1_out, subtractor_1_bout, subtractor_1_out;

  Adder #(.width(1)) adder_1 (.a(A), .b(B), .out(adder_1_out), .cin(Cin), .cout(adder_1_cout));
  Subtractor #(.width(1)) subtractor_1 (.a(A), .b(B), .out(subtractor_1_out), .bin(Cin), .bout(subtractor_1_bout));
  Multiplier #(.width(1)) multiplier_1 (.a(A), .b(B), .out(multiplier_1_out), .cin(Cin), .cout(multiplier_1_cout));
  Comparator #(.width(1), .mode("unsigned")) comparator_1 (
    .a(A), .b(B), .gt(comparator_1_gt), .eq(comparator_1_eq), .lt(comparator_1_lt));
  and and_1 (and_1_out, A, B);
  or or_1 (or_1_out, A, B);
  Multiplexer #(.select(3), .enable("false")) multiplexer_1 (
    .in0(adder_1_cout), .in1(subtractor_1_bout), .in2(multiplier_1_cout), .out(Cout_Bout_Mout), .sel(OPCODE));  // open: in3, in4, in5, in6, in7
  Multiplexer #(.select(3), .enable("false")) multiplexer_2 (
    .in0(adder_1_out), .in1(subtractor_1_out), .in2(multiplier_1_out), .in3(comparator_1_gt),
    .in4(comparator_1_eq), .in5(comparator_1_lt), .in6(and_1_out), .in7(or_1_out), .out(RESULT), .sel(OPCODE));

  // Notes on the sheet:
  //   opcode
  //   000
  //   001
  //   010
  //   011
  //   100
  //   101
  //   110
  //   111
  //   function
  //   ADD
  //   SUB
  //   MUL
  //   GREATER
  //   EQUAL
  //   LESS
  //   AND
  //   OR
endmodule
