// Logisim project 16 bit Alu.circ as structural Verilog
module _16_bit_ALU (
  input  Cin,
  input  [15:0] A,
  input  [15:0] B,
  input  [2:0] OPCODE,
  output out_5,
  output [15:0] out_6
);

  wire n1_bit_alu_1_cout_bout_mout, n1_bit_alu_2_cout_bout_mout, n1_bit_alu_3_cout_bout_mout,
       n1_bit_alu_4_cout_bout_mout, n1_bit_alu_5_cout_bout_mout, n1_bit_alu_6_cout_bout_mout,
       n1_bit_alu_7_cout_bout_mout, n1_bit_alu_8_cout_bout_mout, n1_bit_alu_9_cout_bout_mout,
       n1_bit_alu_10_cout_bout_mout, n1_bit_alu_11_cout_bout_mout, n1_bit_alu_12_cout_bout_mout,
       n1_bit_alu_13_cout_bout_mout, n1_bit_alu_14_cout_bout_mout, n1_bit_alu_15_cout_bout_mout;

  _1_bit_ALU u_1_bit_alu_1 (
    .Cin(Cin), .A(A[0]), .B(B[0]), .Cout_Bout_Mout(n1_bit_alu_1_cout_bout_mout), .RESULT(out_6[0]),
    .OPCODE(OPCODE));
  _1_bit_ALU u_1_bit_alu_2 (
    .Cin(n1_bit_alu_1_cout_bout_mout), .A(A[1]), .B(B[1]), .Cout_Bout_Mout(n1_bit_alu_2_cout_bout_mout),
    .RESULT(out_6[1]), .OPCODE(OPCODE));
  _1_bit_ALU u_1_bit_alu_3 (
    .Cin(n1_bit_alu_2_cout_bout_mout), .A(A[2]), .B(B[2]), .Cout_Bout_Mout(n1_bit_alu_3_cout_bout_mout),
    .RESULT(out_6[2]), .OPCODE(OPCODE));
  _1_bit_ALU u_1_bit_alu_4 (
    .Cin(n1_bit_alu_3_cout_bout_mout), .A(A[3]), .B(B[3]), .Cout_Bout_Mout(n1_bit_alu_4_cout_bout_mout),
    .RESULT(out_6[3]), .OPCODE(OPCODE));
  _1_bit_ALU u_1_bit_alu_5 (
    .Cin(n1_bit_alu_4_cout_bout_mout), .A(A[4]), .B(B[4]), .Cout_Bout_Mout(n1_bit_alu_5_cout_bout_mout),
    .RESULT(out_6[4]), .OPCODE(OPCODE));
  _1_bit_ALU u_1_bit_alu_6 (
    .Cin(n1_bit_alu_5_cout_bout_mout), .A(A[5]), .B(B[5]), .Cout_Bout_Mout(n1_bit_alu_6_cout_bout_mout),
    .RESULT(out_6[5]), .OPCODE(OPCODE));
  _1_bit_ALU u_1_bit_alu_7 (
    .Cin(n1_bit_alu_6_cout_bout_mout), .A(A[6]), .B(B[6]), .Cout_Bout_Mout(n1_bit_alu_7_cout_bout_mout),
    .RESULT(out_6[6]), .OPCODE(OPCODE));
  _1_bit_ALU u_1_bit_alu_8 (
    .Cin(n1_bit_alu_7_cout_bout_mout), .A(A[7]), .B(B[7]), .Cout_Bout_Mout(n1_bit_alu_8_cout_bout_mout),
    .RESULT(out_6[7]), .OPCODE(OPCODE));
  _1_bit_ALU u_1_bit_alu_9 (
    .Cin(n1_bit_alu_8_cout_bout_mout), .A(A[8]), .B(B[8]), .Cout_Bout_Mout(n1_bit_alu_9_cout_bout_mout),
    .RESULT(out_6[8]), .OPCODE(OPCODE));
  _1_bit_ALU u_1_bit_alu_10 (
    .Cin(n1_bit_alu_9_cout_bout_mout), .A(A[9]), .B(B[9]), .Cout_Bout_Mout(n1_bit_alu_10_cout_bout_mout),
    .RESULT(out_6[9]), .OPCODE(OPCODE));
  _1_bit_ALU u_1_bit_alu_11 (
    .Cin(n1_bit_alu_10_cout_bout_mout), .A(A[10]), .B(B[10]), .Cout_Bout_Mout(n1_bit_alu_11_cout_bout_mout),
    .RESULT(out_6[10]), .OPCODE(OPCODE));
  _1_bit_ALU u_1_bit_alu_12 (
    .Cin(n1_bit_alu_11_cout_bout_mout), .A(A[11]), .B(B[11]), .Cout_Bout_Mout(n1_bit_alu_12_cout_bout_mout),
    .RESULT(out_6[11]), .OPCODE(OPCODE));
  _1_bit_ALU u_1_bit_alu_13 (
    .Cin(n1_bit_alu_12_cout_bout_mout), .A(A[12]), .B(B[12]), .Cout_Bout_Mout(n1_bit_alu_13_cout_bout_mout),
    .RESULT(out_6[12]), .OPCODE(OPCODE));
  _1_bit_ALU u_1_bit_alu_14 (
    .Cin(n1_bit_alu_13_cout_bout_mout), .A(A[13]), .B(B[13]), .Cout_Bout_Mout(n1_bit_alu_14_cout_bout_mout),
    .RESULT(out_6[13]), .OPCODE(OPCODE));
  _1_bit_ALU u_1_bit_alu_15 (
    .Cin(n1_bit_alu_14_cout_bout_mout), .A(A[14]), .B(B[14]), .Cout_Bout_Mout(n1_bit_alu_15_cout_bout_mout),
    .RESULT(out_6[14]), .OPCODE(OPCODE));
  _1_bit_ALU u_1_bit_alu_16 (
    .Cin(n1_bit_alu_15_cout_bout_mout), .A(A[15]), .B(B[15]), .Cout_Bout_Mout(out_5), .RESULT(out_6[15]),
    .OPCODE(OPCODE));
endmodule

module _1_bit_ALU (
  input  Cin,
  input  A,
  input  B,
  input  [2:0] OPCODE,
  output Cout_Bout_Mout,
  output RESULT
);

  wire adder_1_cout, adder_1_out, and_1_out, comparator_1_eq, comparator_1_gt, comparator_1_lt,
       multiplier_1_cout, multiplier_1_out, or_1_out, subtractor_1_bout, subtractor_1_out;

  Adder #(.width(1)) adder_1 (.a(A), .b(B), .out(adder_1_out), .cin(Cin), .cout(adder_1_cout));
  Subtractor #(.width(1)) subtractor_1 (.a(A), .b(B), .out(subtractor_1_out), .bin(Cin), .bout(subtractor_1_bout));
  Multiplier #(.width(1)) multiplier_1 (.a(A), .b(B), .out(multiplier_1_out), .cin(Cin), .cout(multiplier_1_cout));
  Comparator #(.width(1), .mode("unsigned")) comparator_1 (
    .a(A), .b(B), .gt(comparator_1_gt), .eq(comparator_1_eq), .lt(comparator_1_lt));
  and and_1 (and_1_out, A, B);
  or or_1 (or_1_out, A, B);
  // XOR_Gate xor_1 is placed but not wired
  Multiplexer #(.select(3), .enable("false")) multiplexer_1 (
    .in0(adder_1_cout), .in1(subtractor_1_bout), .in2(multiplier_1_cout), .out(Cout_Bout_Mout), .sel(OPCODE));  // open: in3, in4, in5, in6, in7
  Multiplexer #(.select(3), .enable("false")) multiplexer_2 (
    .in0(adder_1_out), .in1(subtractor_1_out), .in2(multiplier_1_out), .in3(comparator_1_gt),
    .in4(comparator_1_eq), .in5(comparator_1_lt), .in6(and_1_out), .in7(or_1_out), .out(RESULT), .sel(OPCODE));

  // Notes on the sheet:
  //   opcode
  //   000
  //   001
  //   010
  //   011
  //   100
  //   101
  //   110
  //   111
  //   function
  //   ADD
  //   SUB
  //   MUL
  //   GREATER
  //   EQUAL
  //   LESS
  //   AND
  //   OR
endmodule
