// Logisim project CPU DECODER.circ as structural Verilog
module _16_bit_Register (
  input  [15:0] in_1,
  input  clock
);

  wire [15:0] register_1_q, register_2_q, register_3_q, register_4_q, register_5_q, register_6_q,
       register_7_q, register_8_q, register_9_q, register_10_q, register_11_q, register_12_q, register_13_q,
       register_14_q, register_15_q, register_16_q;

  Register #(.width(16)) register_1 (.Q(register_1_q), .clk(clock));  // open: D, en, clr
  Register #(.width(16)) register_2 (.Q(register_2_q), .clk(clock));  // open: D, en, clr
  Register #(.width(16)) register_3 (.Q(register_3_q), .clk(clock));  // open: D, en, clr
  Register #(.width(16)) register_4 (.Q(register_4_q), .clk(clock));  // open: D, en, clr
  Register #(.width(16)) register_5 (.Q(register_5_q), .clk(clock));  // open: D, en, clr
  Register #(.width(16)) register_6 (.Q(register_6_q), .clk(clock));  // open: D, en, clr
  Register #(.width(16)) register_7 (.Q(register_7_q), .clk(clock));  // open: D, en, clr
  Register #(.width(16)) register_8 (.Q(register_8_q), .clk(clock));  // open: D, en, clr
  Register #(.width(16)) register_9 (.Q(register_9_q), .clk(clock));  // open: D, en, clr
  Register #(.width(16)) register_10 (.Q(register_10_q), .clk(clock));  // open: D, en, clr
  Register #(.width(16)) register_11 (.Q(register_11_q), .clk(clock));  // open: D, en, clr
  Register #(.width(16)) register_12 (.Q(register_12_q), .clk(clock));  // open: D, en, clr
  Register #(.width(16)) register_13 (.Q(register_13_q), .clk(clock));  // open: D, en, clr
  Register #(.width(16)) register_14 (.Q(register_14_q), .clk(clock));  // open: D, en, clr
  Register #(.width(16)) register_15 (.Q(register_15_q), .clk(clock));  // open: D, en, clr
  Register #(.width(16)) register_16 (.Q(register_16_q), .clk(clock));  // open: D, en, clr
  Multiplexer #(.select(4), .width(16)) multiplexer_1 (
    .in0(register_1_q), .in1(register_2_q), .in2(register_3_q), .in3(register_4_q), .in4(register_5_q),
    .in5(register_6_q), .in6(register_7_q), .in7(register_8_q), .in8(register_9_q), .in9(register_10_q),
    .in10(register_11_q), .in11(register_12_q), .in12(register_13_q), .in13(register_14_q),
    .in14(register_15_q), .in15(register_16_q), .out(in_1));  // open: sel, en
endmodule

module cpu_decorder_16bit (
  input  in_1,
  input  in_2,
  input  in_3,
  input  in_4,
  output _0,
  output out_6,
  output _2,
  output out_8
);

  wire and_5_out, not_1_out, not_2_out, not_3_out, not_4_out;

  not not_1 (not_1_out, in_4);
  not not_2 (not_2_out, in_3);
  not not_3 (not_3_out, in_2);
  not not_4 (not_4_out, in_1);
  and and_1 (_0, not_4_out, not_3_out, not_2_out, not_1_out);
  and and_2 (out_6, not_4_out, not_3_out, not_2_out, in_4);
  and and_3 (_2, not_4_out, not_3_out, in_3, not_1_out);
  and and_4 (out_8, not_4_out, not_3_out, in_3, in_4);
  and and_5 (and_5_out, not_4_out, in_2, not_2_out, not_1_out);
  // AND_Gate and_6 has open pins: in0=not_4_out, in1=in_2, in2=not_2_out, in3=in_4, out=open
  // AND_Gate and_7 has open pins: in0=not_4_out, in1=in_2, in2=in_3, in3=not_1_out, out=open
  // AND_Gate and_8 has open pins: in0=not_4_out, in1=in_2, in2=in_3, in3=in_4, out=open
  // AND_Gate and_9 has open pins: in0=in_1, in1=not_3_out, in2=not_2_out, in3=not_1_out, out=open
  // AND_Gate and_10 has open pins: in0=in_1, in1=not_3_out, in2=not_2_out, in3=in_4, out=open
  // AND_Gate and_11 has open pins: in0=in_1, in1=not_3_out, in2=in_3, in3=not_1_out, out=open
  // AND_Gate and_12 has open pins: in0=in_1, in1=not_3_out, in2=in_3, in3=in_4, out=open
  // AND_Gate and_13 has open pins: in0=in_1, in1=in_2, in2=not_2_out, in3=not_1_out, out=open
  // AND_Gate and_14 has open pins: in0=in_1, in1=in_2, in2=not_2_out, in3=in_4, out=open
  // AND_Gate and_15 has open pins: in0=in_1, in1=in_2, in2=in_3, in3=not_1_out, out=open
  // AND_Gate and_16 has open pins: in0=in_1, in1=in_2, in2=in_3, in3=in_4, out=open

  // Notes on the sheet:
  //   5
  //   6
  //   7
  //   8
  //   9
  //   10
  //   10
  //   11
  //   12
  //   13
  //   14
  //   4
  //   3
  //   1
endmodule
