// Logisim project CPU PROJECT.circ as structural Verilog: 17 circuits, main circuit main
module main (
  input  in_1,
  output V,
  output C,
  output N,
  output Z
);

  wire clock_1_out, clock_2_out, clock_3_out, control_unit_1_acc_enable, control_unit_1_acc_set,
       control_unit_1_c_enable, control_unit_1_c_set, control_unit_1_flag_set, control_unit_1_ir_set,
       control_unit_1_mar_set, control_unit_1_pc_enable, control_unit_1_pc_set, control_unit_1_r3_enable,
       control_unit_1_r3_set, control_unit_1_ramd_enable, control_unit_1_ramd_set,
       control_unit_1_rami_enable, control_unit_1_rd_enable, control_unit_1_rd_set, control_unit_1_rs_enable,
       control_unit_1_rs_set, control_unit_1_rt_enable, control_unit_1_rt_set, control_unit_1_tmp_reg_set;
  wire [2:0] control_unit_1_alu_opcode;
  wire [3:0] n16_bit_alu_1_zero;
  wire [15:0] ACC_register_read, adder_1_out, instruction_register_1_register_read,
       memory_address_register_1_register_read, n16_bit_alu_1_result, ram_2_data, TMP_register_read;

  _16_bit_Register TMP (
    .WRITE_enable(control_unit_1_tmp_reg_set), .Register_read(TMP_register_read), .DATA(ACC_register_read));  // open: READ_enable
  _16_bit_ALU u_16_bit_alu_1 (
    .Cin(in_1), .A(ACC_register_read), .B(TMP_register_read), .RESULT(n16_bit_alu_1_result),
    .ZERO(n16_bit_alu_1_zero[0]), .NEGATIVE(n16_bit_alu_1_zero[1]), .CARRY(n16_bit_alu_1_zero[2]),
    .OVERFLOW(n16_bit_alu_1_zero[3]), .OPCODE(control_unit_1_alu_opcode));
  _16_bit_Register ACC (
    .WRITE_enable(control_unit_1_acc_set), .Register_read(ACC_register_read),
    .READ_enable(control_unit_1_acc_enable), .DATA(n16_bit_alu_1_result));
  Flag_Register flag_register_1 (
    .DATA(n16_bit_alu_1_zero), .WRITE_enable(control_unit_1_flag_set), .Register_read({V, C, N, Z}));
  _16_bit_Register rs (
    .WRITE_enable(control_unit_1_rs_set), .Register_read(ACC_register_read),
    .READ_enable(control_unit_1_rs_enable), .DATA(ACC_register_read));
  _16_bit_Register rt (
    .WRITE_enable(control_unit_1_rt_set), .Register_read(ACC_register_read),
    .READ_enable(control_unit_1_rt_enable), .DATA(ACC_register_read));
  _16_bit_Register rd (
    .WRITE_enable(control_unit_1_rd_set), .Register_read(ACC_register_read),
    .READ_enable(control_unit_1_rd_enable), .DATA(ACC_register_read));
  Control_Unit control_unit_1 (
    .PC_ENABLE(control_unit_1_pc_enable), .ACC_ENABLE(control_unit_1_acc_enable),
    .RAMI_ENABLE(control_unit_1_rami_enable), .ALU_OPCODE(control_unit_1_alu_opcode),
    .PC_SET(control_unit_1_pc_set), .ACC_SET(control_unit_1_acc_set), .MAR_SET(control_unit_1_mar_set),
    .RAMD_SET(control_unit_1_ramd_set), .TMP_REG_SET(control_unit_1_tmp_reg_set),
    .FLAG_SET(control_unit_1_flag_set), .INSTRUCTION(instruction_register_1_register_read),
    .rs_enable(control_unit_1_rs_enable), .rt_enable(control_unit_1_rt_enable),
    .rd_enable(control_unit_1_rd_enable), .R3_enable(control_unit_1_r3_enable), .MASTER_CLK(clock_1_out),
    .rs_set(control_unit_1_rs_set), .rt_set(control_unit_1_rt_set), .rd_set(control_unit_1_rd_set),
    .R3_set(control_unit_1_r3_set), .IR_SET(control_unit_1_ir_set), .C_SET(control_unit_1_c_set),
    .C_ENABLE(control_unit_1_c_enable), .RAMD_ENABLE(control_unit_1_ramd_enable));
  Clock #(.highDuration(2), .lowDuration(2)) clock_1 (.out(clock_1_out));
  Instruction_Register instruction_register_1 (
    .DATA(ram_2_data), .WRITE_enable(control_unit_1_ir_set),
    .Register_read(instruction_register_1_register_read));
  _16_bit_Register R3 (
    .WRITE_enable(control_unit_1_r3_set), .Register_read(ACC_register_read),
    .READ_enable(control_unit_1_r3_enable), .DATA(ACC_register_read));
  Memory_Address_Register memory_address_register_1 (
    .DATA(ACC_register_read), .WRITE_enable(control_unit_1_mar_set),
    .Register_read(memory_address_register_1_register_read));
  Program_Counter program_counter_1 (
    .DATA(ACC_register_read), .WRITE_enable(control_unit_1_pc_set), .READ_enable(control_unit_1_pc_enable),
    .Register_read(ACC_register_read));
  Adder #(.width(16)) adder_1 (.a(16'h2), .b(ACC_register_read), .out(adder_1_out));  // open: cin, cout
  RAM #(.addrWidth(16), .dataWidth(16), .bus("separate")) ram_1 (
    .addr(memory_address_register_1_register_read), .din(ACC_register_read), .data(ACC_register_read),
    .str(control_unit_1_ramd_set), .clk(clock_2_out), .ld(control_unit_1_ramd_enable));  // open: sel, clr
  Clock clock_2 (.out(clock_2_out));
  RAM #(.addrWidth(16), .dataWidth(16), .bus("separate")) ram_2 (
    .addr(memory_address_register_1_register_read), .data(ram_2_data), .str(control_unit_1_ramd_set),
    .clk(clock_3_out), .ld(control_unit_1_rami_enable));  // open: din, sel, clr
  Clock clock_3 (.out(clock_3_out));
  _16_bit_Register COUNTER (
    .WRITE_enable(control_unit_1_c_set), .Register_read(ACC_register_read),
    .READ_enable(control_unit_1_c_enable), .DATA(adder_1_out));

  // Notes on the sheet:
  //   DATA
  //   INSTRUCTION
endmodule

module _16_bit_Register (
  input  READ_enable,
  input  [15:0] DATA,
  input  WRITE_enable,
  output [15:0] Register_read
);

  wire [15:0] register_1_q;

  Multiplexer #(.width(16)) multiplexer_1 (
    .in1(register_1_q), .out(Register_read), .sel(1'b1), .en(READ_enable));  // open: in0
  Register #(.width(16)) register_1 (.D(DATA), .en(WRITE_enable), .Q(register_1_q), .clk(WRITE_enable));  // open: clr

  // Notes on the sheet:
  //   data to be written into register
endmodule

module _16_bit_ALU (
  input  Cin,
  input  [15:0] A,
  input  [15:0] B,
  input  [2:0] OPCODE,
  output [15:0] RESULT,
  output ZERO,
  output NEGATIVE,
  output CARRY,
  output OVERFLOW
);

  wire n1_bit_alu_1_cout_bout_mout, n1_bit_alu_2_cout_bout_mout, n1_bit_alu_3_cout_bout_mout,
       n1_bit_alu_4_cout_bout_mout, n1_bit_alu_5_cout_bout_mout, n1_bit_alu_6_cout_bout_mout,
       n1_bit_alu_7_cout_bout_mout, n1_bit_alu_8_cout_bout_mout, n1_bit_alu_9_cout_bout_mout,
       n1_bit_alu_10_cout_bout_mout, n1_bit_alu_11_cout_bout_mout, n1_bit_alu_12_cout_bout_mout,
       n1_bit_alu_13_cout_bout_mout, n1_bit_alu_14_cout_bout_mout, n1_bit_alu_15_cout_bout_mout;

  _1_bit_ALU u_1_bit_alu_1 (
    .Cout_Bout_Mout(n1_bit_alu_1_cout_bout_mout), .Cin(Cin), .RESULT(RESULT[0]), .A(A[0]), .B(B[0]),
    .OPCODE(OPCODE));
  _1_bit_ALU u_1_bit_alu_2 (
    .Cout_Bout_Mout(n1_bit_alu_2_cout_bout_mout), .Cin(n1_bit_alu_1_cout_bout_mout), .RESULT(RESULT[1]),
    .A(A[1]), .B(B[1]), .OPCODE(OPCODE));
  _1_bit_ALU u_1_bit_alu_3 (
    .Cout_Bout_Mout(n1_bit_alu_3_cout_bout_mout), .Cin(n1_bit_alu_2_cout_bout_mout), .RESULT(RESULT[2]),
    .A(A[2]), .B(B[2]), .OPCODE(OPCODE));
  _1_bit_ALU u_1_bit_alu_4 (
    .Cout_Bout_Mout(n1_bit_alu_4_cout_bout_mout), .Cin(n1_bit_alu_3_cout_bout_mout), .RESULT(RESULT[3]),
    .A(A[3]), .B(B[3]), .OPCODE(OPCODE));
  _1_bit_ALU u_1_bit_alu_5 (
    .Cout_Bout_Mout(n1_bit_alu_5_cout_bout_mout), .Cin(n1_bit_alu_4_cout_bout_mout), .RESULT(RESULT[4]),
    .A(A[4]), .B(B[4]), .OPCODE(OPCODE));
  _1_bit_ALU u_1_bit_alu_6 (
    .Cout_Bout_Mout(n1_bit_alu_6_cout_bout_mout), .Cin(n1_bit_alu_5_cout_bout_mout), .RESULT(RESULT[5]),
    .A(A[5]), .B(B[5]), .OPCODE(OPCODE));
  _1_bit_ALU u_1_bit_alu_7 (
    .Cout_Bout_Mout(n1_bit_alu_7_cout_bout_mout), .Cin(n1_bit_alu_6_cout_bout_mout), .RESULT(RESULT[6]),
    .A(A[6]), .B(B[6]), .OPCODE(OPCODE));
  _1_bit_ALU u_1_bit_alu_8 (
    .Cout_Bout_Mout(n1_bit_alu_8_cout_bout_mout), .Cin(n1_bit_alu_7_cout_bout_mout), .RESULT(RESULT[7]),
    .A(A[7]), .B(B[7]), .OPCODE(OPCODE));
  _1_bit_ALU u_1_bit_alu_9 (
    .Cout_Bout_Mout(n1_bit_alu_9_cout_bout_mout), .Cin(n1_bit_alu_8_cout_bout_mout), .RESULT(RESULT[8]),
    .A(A[8]), .B(B[8]), .OPCODE(OPCODE));
  _1_bit_ALU u_1_bit_alu_10 (
    .Cout_Bout_Mout(n1_bit_alu_10_cout_bout_mout), .Cin(n1_bit_alu_9_cout_bout_mout), .RESULT(RESULT[9]),
    .A(A[9]), .B(B[9]), .OPCODE(OPCODE));
  _1_bit_ALU u_1_bit_alu_11 (
    .Cout_Bout_Mout(n1_bit_alu_11_cout_bout_mout), .Cin(n1_bit_alu_10_cout_bout_mout), .RESULT(RESULT[10]),
    .A(A[10]), .B(B[10]), .OPCODE(OPCODE));
  _1_bit_ALU u_1_bit_alu_12 (
    .Cout_Bout_Mout(n1_bit_alu_12_cout_bout_mout), .Cin(n1_bit_alu_11_cout_bout_mout), .RESULT(RESULT[11]),
    .A(A[11]), .B(B[11]), .OPCODE(OPCODE));
  _1_bit_ALU u_1_bit_alu_13 (
    .Cout_Bout_Mout(n1_bit_alu_13_cout_bout_mout), .Cin(n1_bit_alu_12_cout_bout_mout), .RESULT(RESULT[12]),
    .A(A[12]), .B(B[12]), .OPCODE(OPCODE));
  _1_bit_ALU u_1_bit_alu_14 (
    .Cout_Bout_Mout(n1_bit_alu_14_cout_bout_mout), .Cin(n1_bit_alu_13_cout_bout_mout), .RESULT(RESULT[13]),
    .A(A[13]), .B(B[13]), .OPCODE(OPCODE));
  _1_bit_ALU u_1_bit_alu_15 (
    .Cout_Bout_Mout(n1_bit_alu_15_cout_bout_mout), .Cin(n1_bit_alu_14_cout_bout_mout), .RESULT(RESULT[14]),
    .A(A[14]), .B(B[14]), .OPCODE(OPCODE));
  _1_bit_ALU u_1_bit_alu_16 (
    .Cout_Bout_Mout(CARRY), .Cin(n1_bit_alu_15_cout_bout_mout), .RESULT(NEGATIVE), .A(A[15]), .B(B[15]),
    .OPCODE(OPCODE));
  xor xor_1 (OVERFLOW, n1_bit_alu_15_cout_bout_mout, CARRY);
  nor nor_1 (ZERO, RESULT[0], RESULT[1], RESULT[2], RESULT[3], RESULT[4], RESULT[5], RESULT[6], RESULT[7], RESULT[8], RESULT[9], RESULT[10], RESULT[11], RESULT[12], RESULT[13], RESULT[14], NEGATIVE);

  assign RESULT[15] = NEGATIVE;

  // Notes on the sheet:
  //   000
  //   001
  //   010
  //   011
  //   100
  //   101
  //   110
  //   111
  //   opcode
  //   ADD
  //   SUB
  //   AND
  //   OR
  //   XOR
  //   function
endmodule

module Control_Unit (
  input  MASTER_CLK,
  input  [15:0] INSTRUCTION,
  output RAMD_ENABLE,
  output C_SET,
  output C_ENABLE,
  output PC_SET,
  output PC_ENABLE,
  output ACC_SET,
  output ACC_ENABLE,
  output MAR_SET,
  output RAMI_ENABLE,
  output RAMD_SET,
  output rs_enable,
  output IR_SET,
  output rt_enable,
  output TMP_REG_SET,
  output rd_enable,
  output FLAG_SET,
  output R3_enable,
  output rs_set,
  output rt_set,
  output rd_set,
  output R3_set,
  output [2:0] ALU_OPCODE
);

  wire and_1_out, and_2_out, and_3_out, and_4_out, and_5_out, and_6_out, and_7_out, and_8_out, and_9_out,
       and_10_out, and_11_out, and_12_out, and_13_out, and_14_out, and_15_out, and_16_out, and_17_out,
       and_18_out, and_21_out, and_22_out, and_23_out, and_24_out, and_25_out, and_26_out, and_27_out,
       and_28_out, and_29_out, and_30_out, and_31_out, and_32_out, and_33_out, clocks_1_enable_clk,
       clocks_1_main_clock, clocks_1_set_clk, decoder_1_out0, decoder_1_out1, decoder_1_out2, decoder_1_out3,
       decoder_2_out0, decoder_2_out1, decoder_2_out2, decoder_2_out3, decoder_3_out0, decoder_3_out1,
       decoder_3_out2, decoder_3_out3, decoder_4_out0, decoder_4_out1, decoder_4_out2, decoder_4_out3,
       decoder_4_out4, decoder_4_out5, decoder_4_out6, decoder_4_out7, decoder_5_out0, decoder_5_out1,
       decoder_5_out2, decoder_5_out3, decoder_6_out0, decoder_6_out1, decoder_6_out2, decoder_6_out3,
       decoder_7_out0, decoder_7_out1, decoder_7_out2, decoder_7_out3, not_1_out, or_1_out, or_2_out,
       or_3_out, or_4_out, or_5_out, or_6_out, or_7_out, or_8_out, or_9_out, R0_2_out, R0_3_out, R0_4_out,
       R1_2_out, R1_3_out, R1_4_out, R2_2_out, R2_3_out, R2_4_out, R3_2_out, R3_3_out, R3_4_out,
       step_controller_1__1, step_controller_1__2, step_controller_1__3, step_controller_1__4,
       step_controller_1__5, step_controller_1__6;

  or R0 (rs_enable, and_1_out, and_5_out, and_9_out);
  or R1 (rt_enable, and_2_out, and_6_out, and_10_out);
  or R2 (rd_enable, and_3_out, and_7_out, and_11_out);
  or R3 (R3_enable, and_4_out, and_8_out, and_12_out);
  and RAMD (RAMD_ENABLE, clocks_1_enable_clk, and_23_out);
  and C (C_ENABLE, clocks_1_enable_clk, step_controller_1__2);
  and PC (PC_ENABLE, clocks_1_enable_clk, or_1_out);
  or or_1 (or_1_out, step_controller_1__1, and_27_out);
  and ACC (ACC_ENABLE, clocks_1_enable_clk, or_2_out);
  or or_2 (or_2_out, and_31_out, and_32_out);
  and RAMI (RAMI_ENABLE, clocks_1_enable_clk, or_3_out);
  or or_3 (or_3_out, step_controller_1__2, and_28_out);
  and and_1 (and_1_out, decoder_1_out0, or_5_out, clocks_1_enable_clk);
  and and_2 (and_2_out, decoder_1_out1, or_5_out, clocks_1_enable_clk);
  and and_3 (and_3_out, decoder_1_out2, or_5_out, clocks_1_enable_clk);
  and and_4 (and_4_out, decoder_1_out3, or_5_out, clocks_1_enable_clk);
  and and_5 (and_5_out, decoder_2_out0, or_4_out, clocks_1_enable_clk);
  and and_6 (and_6_out, decoder_2_out1, or_4_out, clocks_1_enable_clk);
  and and_7 (and_7_out, decoder_2_out2, or_4_out, clocks_1_enable_clk);
  and and_8 (and_8_out, decoder_2_out3, or_4_out, clocks_1_enable_clk);
  and and_9 (and_9_out, decoder_3_out0, or_6_out, clocks_1_enable_clk);
  and and_10 (and_10_out, decoder_3_out1, or_6_out, clocks_1_enable_clk);
  and and_11 (and_11_out, decoder_3_out2, or_6_out, clocks_1_enable_clk);
  and and_12 (and_12_out, decoder_3_out3, or_6_out, clocks_1_enable_clk);
  and ALU (ALU_OPCODE[0], and_33_out, INSTRUCTION[12], INSTRUCTION[15]);
  and ALU_2 (ALU_OPCODE[1], and_33_out, INSTRUCTION[13], INSTRUCTION[15]);
  and ALU_3 (ALU_OPCODE[2], and_33_out, INSTRUCTION[14], INSTRUCTION[15]);
  Decoder #(.select(4), .enable("false")) decoder_1 (
    .out0(decoder_1_out0), .out1(decoder_1_out1), .out2(decoder_1_out2), .out3(decoder_1_out3),
    .sel(INSTRUCTION[11:8]));  // open: out4, out5, out6, out7, out8, out9, out10, out11, out12, out13, out14, out15
  or or_4 (or_4_out, and_33_out, and_22_out, and_21_out);
  Decoder #(.select(4), .enable("false")) decoder_2 (
    .out0(decoder_2_out0), .out1(decoder_2_out1), .out2(decoder_2_out2), .out3(decoder_2_out3),
    .sel(INSTRUCTION[7:4]));  // open: out4, out5, out6, out7, out8, out9, out10, out11, out12, out13, out14, out15
  Decoder #(.select(4), .enable("false")) decoder_3 (
    .out0(decoder_3_out0), .out1(decoder_3_out1), .out2(decoder_3_out2), .out3(decoder_3_out3),
    .sel(INSTRUCTION[3:0]));  // open: out4, out5, out6, out7, out8, out9, out10, out11, out12, out13, out14, out15
  CLOCKS clocks_1 (
    .SYS_CLK_IN(MASTER_CLK), .MAIN_CLOCK(clocks_1_main_clock), .SET_CLK(clocks_1_set_clk),
    .ENABLE_CLK(clocks_1_enable_clk));
  or or_5 (or_5_out, and_25_out, and_29_out);
  Decoder #(.select(3), .enable("false")) decoder_4 (
    .out0(decoder_4_out0), .out1(decoder_4_out1), .out2(decoder_4_out2), .out3(decoder_4_out3),
    .out4(decoder_4_out4), .out5(decoder_4_out5), .out6(decoder_4_out6), .out7(decoder_4_out7),
    .sel(INSTRUCTION[14:12]));
  not not_1 (not_1_out, INSTRUCTION[15]);
  STEP_CONTROLLER step_controller_1 (
    ._1(step_controller_1__1), ._2(step_controller_1__2), ._3(step_controller_1__3),
    ._4(step_controller_1__4), ._5(step_controller_1__5), ._6(step_controller_1__6),
    .CLOCK(clocks_1_main_clock));
  and and_13 (and_13_out, not_1_out, decoder_4_out0);
  and and_14 (and_14_out, not_1_out, decoder_4_out1);
  and and_15 (and_15_out, not_1_out, decoder_4_out2);
  and and_16 (and_16_out, not_1_out, decoder_4_out3);
  and and_17 (and_17_out, not_1_out, decoder_4_out4);
  and and_18 (and_18_out, not_1_out, decoder_4_out5);
  // AND_Gate and_19 has open pins: in0=not_1_out, in1=decoder_4_out6, out=open
  // AND_Gate and_20 has open pins: in0=not_1_out, in1=decoder_4_out7, out=open
  and and_21 (and_21_out, step_controller_1__3, and_13_out);
  and and_22 (and_22_out, step_controller_1__3, and_14_out);
  or or_6 (or_6_out, and_24_out, and_26_out);
  and and_23 (and_23_out, step_controller_1__4, and_13_out);
  and and_24 (and_24_out, step_controller_1__4, and_14_out);
  and and_25 (and_25_out, step_controller_1__3, and_15_out);
  and and_26 (and_26_out, step_controller_1__3, and_16_out);
  and and_27 (and_27_out, step_controller_1__3, and_17_out);
  and and_28 (and_28_out, step_controller_1__4, and_17_out);
  and and_29 (and_29_out, step_controller_1__4, INSTRUCTION[15]);
  and and_30 (and_30_out, step_controller_1__4, and_18_out);
  and and_31 (and_31_out, step_controller_1__5, and_18_out);
  and and_32 (and_32_out, step_controller_1__6, INSTRUCTION[15]);
  and and_33 (and_33_out, INSTRUCTION[15], step_controller_1__5);
  Decoder #(.select(4), .enable("false")) decoder_5 (
    .out0(decoder_5_out0), .out1(decoder_5_out1), .out2(decoder_5_out2), .out3(decoder_5_out3),
    .sel(INSTRUCTION[11:8]));  // open: out4, out5, out6, out7, out8, out9, out10, out11, out12, out13, out14, out15
  Decoder #(.select(4), .enable("false")) decoder_6 (
    .out0(decoder_6_out0), .out1(decoder_6_out1), .out2(decoder_6_out2), .out3(decoder_6_out3),
    .sel(INSTRUCTION[7:4]));  // open: out4, out5, out6, out7, out8, out9, out10, out11, out12, out13, out14, out15
  or or_7 (or_7_out, and_23_out, and_32_out);
  Decoder #(.select(4), .enable("false")) decoder_7 (
    .out0(decoder_7_out0), .out1(decoder_7_out1), .out2(decoder_7_out2), .out3(decoder_7_out3),
    .sel(INSTRUCTION[3:0]));  // open: out4, out5, out6, out7, out8, out9, out10, out11, out12, out13, out14, out15
  or or_8 (or_8_out, step_controller_1__2, and_28_out, and_26_out, and_31_out);
  or or_9 (or_9_out, step_controller_1__1, and_22_out, and_21_out, and_27_out);
  and C_2 (C_SET, clocks_1_set_clk, step_controller_1__1);
  and PC_2 (PC_SET, clocks_1_set_clk, or_8_out);
  and ACC_2 (ACC_SET, clocks_1_set_clk, and_33_out);
  and MAR (MAR_SET, clocks_1_set_clk, or_9_out);
  and RAMD_2 (RAMD_SET, clocks_1_set_clk, and_24_out);
  and IR (IR_SET, clocks_1_set_clk, step_controller_1__2);
  and TMP (TMP_REG_SET, clocks_1_set_clk, and_29_out);
  and FLG (FLAG_SET, clocks_1_set_clk, and_33_out);
  and R0_2 (R0_2_out, decoder_5_out0, 1'b0, clocks_1_set_clk);
  and R1_2 (R1_2_out, decoder_5_out1, 1'b0, clocks_1_set_clk);
  and R2_2 (R2_2_out, decoder_5_out2, 1'b0, clocks_1_set_clk);
  and R3_2 (R3_2_out, decoder_5_out3, 1'b0, clocks_1_set_clk);
  and R0_3 (R0_3_out, decoder_6_out0, and_25_out, clocks_1_set_clk);
  and R1_3 (R1_3_out, decoder_6_out1, and_25_out, clocks_1_set_clk);
  and R2_3 (R2_3_out, decoder_6_out2, and_25_out, clocks_1_set_clk);
  and R3_3 (R3_3_out, decoder_6_out3, and_25_out, clocks_1_set_clk);
  and R0_4 (R0_4_out, decoder_7_out0, or_7_out, clocks_1_set_clk);
  and R1_4 (R1_4_out, decoder_7_out1, or_7_out, clocks_1_set_clk);
  and R2_4 (R2_4_out, decoder_7_out2, or_7_out, clocks_1_set_clk);
  and R3_4 (R3_4_out, decoder_7_out3, or_7_out, clocks_1_set_clk);
  or or_10 (rs_set, R0_2_out, R0_3_out, R0_4_out);
  or or_11 (rt_set, R1_2_out, R1_3_out, R1_4_out);
  or or_12 (rd_set, R2_2_out, R2_3_out, R2_4_out);
  or or_13 (R3_set, R3_2_out, R3_3_out, R3_4_out);

  // Notes on the sheet:
  //   ENABLE
  //   SET
endmodule

module CLOCKS (
  input  SYS_CLK_IN,
  output MAIN_CLOCK,
  output SET_CLK,
  output ENABLE_CLK
);

  wire j_k_ff_1_q, j_k_ff_1_qn, not_1_out, xor_1_out;

  not not_1 (not_1_out, SYS_CLK_IN);
  J_K_Flip_Flop j_k_ff_1 (
    .J(1'b1), .clk(not_1_out), .K(1'b1), .Q(j_k_ff_1_q), .Qn(j_k_ff_1_qn), .en(1'b1));  // open: preset, reset
  and and_1 (SET_CLK, not_1_out, j_k_ff_1_q);
  nand nand_1 (ENABLE_CLK, j_k_ff_1_qn, not_1_out);
  xor xor_1 (xor_1_out, j_k_ff_1_q, ENABLE_CLK);
  or or_1 (MAIN_CLOCK, xor_1_out, SET_CLK);
endmodule

module Instruction_Register (
  input  [15:0] DATA,
  input  WRITE_enable,
  output [15:0] Register_read
);

  Register #(.width(16)) register_1 (.D(DATA), .en(WRITE_enable), .Q(Register_read), .clk(WRITE_enable));  // open: clr

  // Notes on the sheet:
  //   data to be written into register
endmodule

module Memory_Address_Register (
  input  [15:0] DATA,
  input  WRITE_enable,
  output [15:0] Register_read
);

  Register #(.width(16)) register_1 (.D(DATA), .en(WRITE_enable), .Q(Register_read), .clk(WRITE_enable));  // open: clr

  // Notes on the sheet:
  //   data to be written into register
endmodule

module PC_INCREMENT (
  input  [15:0] INPUT_FROM_PC,
  output [15:0] OUTPUT_TO_ACC
);

  Adder #(.width(16)) adder_1 (.a(16'h1), .b(INPUT_FROM_PC), .out(OUTPUT_TO_ACC), .cin(1'b0));  // open: cout
endmodule

module Program_Counter (
  input  READ_enable,
  input  [15:0] DATA,
  input  WRITE_enable,
  output [15:0] Register_read
);

  wire [15:0] register_1_q;

  Multiplexer #(.width(16)) multiplexer_1 (
    .in1(register_1_q), .out(Register_read), .sel(1'b1), .en(READ_enable));  // open: in0
  Register #(.width(16)) register_1 (.D(DATA), .en(WRITE_enable), .Q(register_1_q), .clk(WRITE_enable));  // open: clr

  // Notes on the sheet:
  //   data to be written into register
endmodule

module STEP_CONTROLLER (
  input  CLOCK,
  output _1,
  output _2,
  output _3,
  output _4,
  output _5,
  output _6
);

  wire not_1_out, not_2_out, not_3_out, not_4_out, not_5_out, not_6_out, not_7_out, not_8_out, or_2_out,
       or_3_out, register_1_q, register_2_q, register_3_q, register_4_q, register_5_q, register_6_q,
       register_7_q, register_8_q, register_9_q, register_10_q, register_11_q, register_12_q;

  not not_1 (not_1_out, CLOCK);
  or or_1 (_1, register_12_q, not_3_out);
  not not_2 (not_2_out, register_12_q);
  Register #(.width(1)) register_1 (
    .D(not_2_out), .en(or_2_out), .Q(register_1_q), .clk(or_2_out), .clr(register_12_q));
  or or_2 (or_2_out, not_1_out, register_12_q);
  or or_3 (or_3_out, CLOCK, register_12_q);
  not not_3 (not_3_out, register_2_q);
  Register #(.width(1)) register_2 (
    .D(register_1_q), .en(or_3_out), .Q(register_2_q), .clk(or_3_out), .clr(register_12_q));
  Register #(.width(1)) register_3 (
    .D(register_2_q), .en(or_2_out), .Q(register_3_q), .clk(or_2_out), .clr(register_12_q));
  and and_1 (_2, register_2_q, not_4_out);
  not not_4 (not_4_out, register_4_q);
  Register #(.width(1)) register_4 (
    .D(register_3_q), .en(or_3_out), .Q(register_4_q), .clk(or_3_out), .clr(register_12_q));
  Register #(.width(1)) register_5 (
    .D(register_4_q), .en(or_2_out), .Q(register_5_q), .clk(or_2_out), .clr(register_12_q));
  and and_2 (_3, register_4_q, not_5_out);
  not not_5 (not_5_out, register_6_q);
  Register #(.width(1)) register_6 (
    .D(register_5_q), .en(or_3_out), .Q(register_6_q), .clk(or_3_out), .clr(register_12_q));
  Register #(.width(1)) register_7 (
    .D(register_6_q), .en(or_2_out), .Q(register_7_q), .clk(or_2_out), .clr(register_12_q));
  and and_3 (_4, register_6_q, not_6_out);
  not not_6 (not_6_out, register_8_q);
  Register #(.width(1)) register_8 (
    .D(register_7_q), .en(or_3_out), .Q(register_8_q), .clk(or_3_out), .clr(register_12_q));
  and and_4 (_5, register_8_q, not_7_out);
  Register #(.width(1)) register_9 (
    .D(register_8_q), .en(or_2_out), .Q(register_9_q), .clk(or_2_out), .clr(register_12_q));
  not not_7 (not_7_out, register_10_q);
  Register #(.width(1)) register_10 (
    .D(register_9_q), .en(or_3_out), .Q(register_10_q), .clk(or_3_out), .clr(register_12_q));
  and and_5 (_6, register_10_q, not_8_out);
  Register #(.width(1)) register_11 (
    .D(register_10_q), .en(or_2_out), .Q(register_11_q), .clk(or_2_out), .clr(register_12_q));
  not not_8 (not_8_out, register_12_q);
  Register #(.width(1)) register_12 (
    .D(register_11_q), .en(or_3_out), .Q(register_12_q), .clk(or_3_out), .clr(register_12_q));
endmodule

module Flag_Register (
  input  [3:0] DATA,
  input  WRITE_enable,
  output [3:0] Register_read
);

  Register #(.width(4)) register_1 (.D(DATA), .en(WRITE_enable), .Q(Register_read), .clk(WRITE_enable));  // open: clr

  // Notes on the sheet:
  //   data to be written into register
endmodule

module _16_bit_RIGHT_shifter (
  input  [15:0] in_1,
  output [15:0] out_2
);

  wire clock_1_out;
  wire [15:0] register_1_q;

  Register #(.width(16)) register_1 (.D(in_1), .en(clock_1_out), .Q(register_1_q), .clk(clock_1_out));  // open: clr
  Clock clock_1 (.out(clock_1_out));
  Register #(.width(16)) register_2 (
    .D({register_1_q[0], register_1_q[15:1]}), .en(clock_1_out), .Q(out_2), .clk(clock_1_out));  // open: clr
endmodule

module _16_bit_LEFT_shifter (
  input  [15:0] in_1,
  output [15:0] out_2
);

  wire clock_1_out;
  wire [15:0] register_1_q;

  Register #(.width(16)) register_1 (.D(in_1), .en(clock_1_out), .Q(register_1_q), .clk(clock_1_out));  // open: clr
  Clock clock_1 (.out(clock_1_out));
  Register #(.width(16)) register_2 (
    .D({register_1_q[14:0], register_1_q[15]}), .en(clock_1_out), .Q(out_2), .clk(clock_1_out));  // open: clr
endmodule

module _1_bit_ALU (
  input  Cin,
  input  A,
  input  B,
  input  [2:0] OPCODE,
  output Cout_Bout_Mout,
  output RESULT
);

  wire adder_1_cout, adder_1_out, and_1_out, nand_1_out, not_1_out, or_1_out, subtractor_1_bout,
       subtractor_1_out, xnor_1_out, xor_1_out;

  and and_1 (and_1_out, A, B);
  or or_1 (or_1_out, A, B);
  xor xor_1 (xor_1_out, A, B);
  not not_1 (not_1_out, A);
  xnor xnor_1 (xnor_1_out, A, B);
  nand nand_1 (nand_1_out, A, B);
  Adder #(.width(1)) adder_1 (.a(A), .b(B), .out(adder_1_out), .cin(Cin), .cout(adder_1_cout));
  Subtractor #(.width(1)) subtractor_1 (.a(A), .b(B), .out(subtractor_1_out), .bin(Cin), .bout(subtractor_1_bout));
  Multiplexer #(.enable("false")) multiplexer_1 (
    .in0(adder_1_cout), .in1(subtractor_1_bout), .out(Cout_Bout_Mout), .sel(OPCODE[0]));
  Multiplexer #(.select(3), .enable("false")) multiplexer_2 (
    .in0(adder_1_out), .in1(subtractor_1_out), .in2(and_1_out), .in3(or_1_out), .in4(xor_1_out),
    .in5(not_1_out), .in6(xnor_1_out), .in7(nand_1_out), .out(RESULT), .sel(OPCODE));

  // Notes on the sheet:
  //   opcode
  //   000
  //   001
  //   010
  //   011
  //   100
  //   101
  //   110
  //   111
  //   function
  //   ADD
  //   SUB
  //   AND
  //   OR
  //   XOR
endmodule

module _16_bit_REGISTER_FILE (
  input  [3:0] SELECT_Register_read_1,
  input  READ_enable,
  input  [3:0] SELECT_Register_read_2,
  input  [3:0] SELECT_Register_write,
  input  [15:0] DATA,
  input  WRITE_enable,
  output [15:0] Register_read_1,
  output [15:0] Register_read_2
);

  wire and_1_out, and_2_out, and_3_out, and_4_out, and_5_out, and_6_out, and_7_out, and_8_out, and_9_out,
       and_10_out, and_11_out, and_12_out, and_13_out, and_14_out, and_15_out, and_16_out, decoder_1_out0,
       decoder_1_out1, decoder_1_out2, decoder_1_out3, decoder_1_out4, decoder_1_out5, decoder_1_out6,
       decoder_1_out7, decoder_1_out8, decoder_1_out9, decoder_1_out10, decoder_1_out11, decoder_1_out12,
       decoder_1_out13, decoder_1_out14, decoder_1_out15;
  wire [15:0] register_1_q, register_2_q, register_3_q, register_4_q, register_5_q, register_6_q,
       register_7_q, register_8_q, register_9_q, register_10_q, register_11_q, register_12_q, register_13_q,
       register_14_q, register_15_q, register_16_q;

  Decoder #(.select(4), .enable("false")) decoder_1 (
    .out0(decoder_1_out0), .out1(decoder_1_out1), .out2(decoder_1_out2), .out3(decoder_1_out3),
    .out4(decoder_1_out4), .out5(decoder_1_out5), .out6(decoder_1_out6), .out7(decoder_1_out7),
    .out8(decoder_1_out8), .out9(decoder_1_out9), .out10(decoder_1_out10), .out11(decoder_1_out11),
    .out12(decoder_1_out12), .out13(decoder_1_out13), .out14(decoder_1_out14), .out15(decoder_1_out15),
    .sel(SELECT_Register_write));
  and and_1 (and_1_out, decoder_1_out0, WRITE_enable);
  and and_2 (and_2_out, decoder_1_out1, WRITE_enable);
  and and_3 (and_3_out, decoder_1_out2, WRITE_enable);
  and and_4 (and_4_out, decoder_1_out3, WRITE_enable);
  and and_5 (and_5_out, decoder_1_out4, WRITE_enable);
  and and_6 (and_6_out, decoder_1_out5, WRITE_enable);
  and and_7 (and_7_out, decoder_1_out6, WRITE_enable);
  and and_8 (and_8_out, decoder_1_out7, WRITE_enable);
  and and_9 (and_9_out, decoder_1_out8, WRITE_enable);
  and and_10 (and_10_out, decoder_1_out9, WRITE_enable);
  and and_11 (and_11_out, decoder_1_out10, WRITE_enable);
  and and_12 (and_12_out, decoder_1_out11, WRITE_enable);
  and and_13 (and_13_out, decoder_1_out12, WRITE_enable);
  and and_14 (and_14_out, decoder_1_out13, WRITE_enable);
  and and_15 (and_15_out, decoder_1_out14, WRITE_enable);
  and and_16 (and_16_out, decoder_1_out15, WRITE_enable);
  Register #(.width(16)) register_1 (.D(DATA), .en(and_1_out), .Q(register_1_q), .clk(and_1_out));  // open: clr
  Register #(.width(16)) register_2 (.D(DATA), .en(and_2_out), .Q(register_2_q), .clk(and_2_out));  // open: clr
  Register #(.width(16)) register_3 (.D(DATA), .en(and_3_out), .Q(register_3_q), .clk(and_3_out));  // open: clr
  Register #(.width(16)) register_4 (.D(DATA), .en(and_4_out), .Q(register_4_q), .clk(and_4_out));  // open: clr
  Register #(.width(16)) register_5 (.D(DATA), .en(and_5_out), .Q(register_5_q), .clk(and_5_out));  // open: clr
  Register #(.width(16)) register_6 (.D(DATA), .en(and_6_out), .Q(register_6_q), .clk(and_6_out));  // open: clr
  Register #(.width(16)) register_7 (.D(DATA), .en(and_7_out), .Q(register_7_q), .clk(and_7_out));  // open: clr
  Register #(.width(16)) register_8 (.D(DATA), .en(and_8_out), .Q(register_8_q), .clk(and_8_out));  // open: clr
  Register #(.width(16)) register_9 (.D(DATA), .en(and_9_out), .Q(register_9_q), .clk(and_9_out));  // open: clr
  Register #(.width(16)) register_10 (.D(DATA), .en(and_10_out), .Q(register_10_q), .clk(and_10_out));  // open: clr
  Register #(.width(16)) register_11 (.D(DATA), .en(and_11_out), .Q(register_11_q), .clk(and_11_out));  // open: clr
  Register #(.width(16)) register_12 (.D(DATA), .en(and_12_out), .Q(register_12_q), .clk(and_12_out));  // open: clr
  Register #(.width(16)) register_13 (.D(DATA), .en(and_13_out), .Q(register_13_q), .clk(and_13_out));  // open: clr
  Register #(.width(16)) register_14 (.D(DATA), .en(and_14_out), .Q(register_14_q), .clk(and_14_out));  // open: clr
  Register #(.width(16)) register_15 (.D(DATA), .en(and_15_out), .Q(register_15_q), .clk(and_15_out));  // open: clr
  Register #(.width(16)) register_16 (.D(DATA), .en(and_16_out), .Q(register_16_q), .clk(and_16_out));  // open: clr
  Multiplexer #(.select(4), .width(16)) multiplexer_1 (
    .in0(register_1_q), .in1(register_2_q), .in2(register_3_q), .in3(register_4_q), .in4(register_5_q),
    .in5(register_6_q), .in6(register_7_q), .in7(register_8_q), .in8(register_9_q), .in9(register_10_q),
    .in10(register_11_q), .in11(register_12_q), .in12(register_13_q), .in13(register_14_q),
    .in14(register_15_q), .in15(register_16_q), .out(Register_read_1), .sel(SELECT_Register_read_1),
    .en(READ_enable));
  Multiplexer #(.select(4), .width(16)) multiplexer_2 (
    .in0(register_1_q), .in1(register_2_q), .in2(register_3_q), .in3(register_4_q), .in4(register_5_q),
    .in5(register_6_q), .in6(register_7_q), .in7(register_8_q), .in8(register_9_q), .in9(register_10_q),
    .in10(register_11_q), .in11(register_12_q), .in12(register_13_q), .in13(register_14_q),
    .in14(register_15_q), .in15(register_16_q), .out(Register_read_2), .sel(SELECT_Register_read_2),
    .en(READ_enable));

  // Notes on the sheet:
  //   Read from which Register?
  //   Read from which Register?
  //   write into which register?
  //   data to be written into register
endmodule

module TWO_16_bit_Registers (
  input  READ_enable,
  input  SELECT_Register_read_1,
  input  SELECT_Register_read_2,
  input  SELECT_Register_write,
  input  [15:0] DATA,
  input  WRITE_enable,
  input  RESET,
  output [15:0] Register_read_1,
  output [15:0] Register_read_2
);

  wire and_1_out, and_2_out, decoder_1_out0, decoder_1_out1;
  wire [15:0] register_1_q, register_2_q;

  Decoder #(.enable("false")) decoder_1 (.out0(decoder_1_out0), .out1(decoder_1_out1), .sel(SELECT_Register_write));
  and and_1 (and_1_out, decoder_1_out0, WRITE_enable);
  and and_2 (and_2_out, decoder_1_out1, WRITE_enable);
  Register #(.width(16)) register_1 (.D(DATA), .en(and_1_out), .Q(register_1_q), .clk(and_1_out), .clr(RESET));
  Register #(.width(16)) register_2 (.D(DATA), .en(and_2_out), .Q(register_2_q), .clk(and_2_out), .clr(RESET));
  Multiplexer #(.width(16)) multiplexer_1 (
    .in0(register_1_q), .in1(register_2_q), .out(Register_read_1), .sel(SELECT_Register_read_1),
    .en(READ_enable));
  Multiplexer #(.width(16)) multiplexer_2 (
    .in0(register_1_q), .in1(register_2_q), .out(Register_read_2), .sel(SELECT_Register_read_2),
    .en(READ_enable));

  // Notes on the sheet:
  //   Read from which Register?
  //   Read from which Register?
  //   write into which register?
  //   data to be written into register
endmodule

module THE_ONER (
  input  [15:0] INPUT,
  input  in_2,
  output [15:0] OUTPUT
);

  wire not_1_out;

  and and_1 (OUTPUT[15], INPUT[15], not_1_out);
  and and_2 (OUTPUT[14], INPUT[14], not_1_out);
  and and_3 (OUTPUT[12], INPUT[12], not_1_out);
  and and_4 (OUTPUT[13], INPUT[13], not_1_out);
  and and_5 (OUTPUT[11], INPUT[11], not_1_out);
  and and_6 (OUTPUT[10], INPUT[10], not_1_out);
  and and_7 (OUTPUT[9], INPUT[9], not_1_out);
  and and_8 (OUTPUT[8], INPUT[8], not_1_out);
  and and_9 (OUTPUT[7], INPUT[7], not_1_out);
  and and_10 (OUTPUT[6], INPUT[6], not_1_out);
  and and_11 (OUTPUT[4], INPUT[4], not_1_out);
  and and_12 (OUTPUT[5], INPUT[5], not_1_out);
  and and_13 (OUTPUT[3], INPUT[3], not_1_out);
  and and_14 (OUTPUT[2], INPUT[2], not_1_out);
  and and_15 (OUTPUT[1], INPUT[1], not_1_out);
  or or_1 (OUTPUT[0], INPUT[0], in_2);
  not not_1 (not_1_out, in_2);
endmodule
