// Logisim project full adder & subtractor.circ as structural Verilog: 1 circuit, main circuit full adder & subtractor
module full_adder___subtractor (
  input  Cin,
  input  A,
  input  B,
  output SUM,
  output CARRY_OUT
);

  wire and_1_out, and_2_out, xor_1_out, xor_2_out;

  xor xor_1 (xor_1_out, B, Cin);
  xor xor_2 (xor_2_out, A, xor_1_out);
  and and_1 (and_1_out, A, xor_1_out);
  xor xor_3 (SUM, Cin, xor_2_out);
  and and_2 (and_2_out, Cin, xor_2_out);
  or or_1 (CARRY_OUT, and_2_out, and_1_out);
endmodule
