// Logisim project full adder.circ as structural Verilog: 1 circuit, main circuit full adder
module full_adder (
  input  Cin,
  input  A,
  input  B,
  output SUM,
  output CARRY_OUT
);

  wire and_1_out, and_2_out, xor_1_out;

  xor xor_1 (xor_1_out, A, B);
  and and_1 (and_1_out, A, B);
  xor xor_2 (SUM, Cin, xor_1_out);
  and and_2 (and_2_out, Cin, xor_1_out);
  or or_1 (CARRY_OUT, and_2_out, and_1_out);
endmodule
